# Fritzing sketch hoeveel-heb-je-op (saved by Fritzing 0.9.10b)
breadboards: 3

parts:
  M1 = ESP32-S3-DevKitC-1 [part_number=ESP32-S3-DevKitC-1]
  S1 = Momentary Switch [package=ksa_sealed_tac_switch]
  R1 = Resistor [tolerance=±5% power=0.25 resistance=330 package=THT]
  S2 = Momentary Switch [package=ksa_sealed_tac_switch]
  R2 = Resistor [tolerance=±5% power=0.25 resistance=330 package=THT]
  D1 = LED_BARGRAPH_10 [package=led_bargaph_10]
  R3 = Resistor [tolerance=±5% power=0.25 resistance=330 package=THT]
  R4 = Resistor [tolerance=±5% power=0.25 resistance=330 package=THT]
  R5 = Resistor [tolerance=±5% power=0.25 resistance=330 package=THT]
  R6 = Resistor [tolerance=±5% power=0.25 resistance=330 package=THT]
  R7 = Resistor [tolerance=±5% power=0.25 resistance=330 package=THT]
  R8 = Resistor [tolerance=±5% power=0.25 resistance=330 package=THT]
  R9 = Resistor [tolerance=±5% power=0.25 resistance=330 package=THT]
  R10 = Resistor [tolerance=±5% power=0.25 resistance=330 package=THT]
  R11 = Resistor [tolerance=±5% power=0.25 resistance=330 package=THT]
  R12 = Resistor [tolerance=±5% power=0.25 resistance=330 package=THT]

nets:
  N1: M1.pin_1, M1.pin_2, S1.1, S2.1
  N2: M1.pin_5, S1.4, R1.Pin_1
  N3: M1.pin_6, S2.4, R2.Pin_1
  N4: M1.pin_8, D1.A_C
  N5: M1.pin_9, D1.B_C
  N6: M1.pin_10, D1.C_C
  N7: M1.pin_11, D1.D_C
  N8: M1.pin_12, D1.E_C
  N9: M1.pin_13, D1.F_C
  N10: M1.pin_14, D1.G_C
  N11: M1.pin_15, D1.H_C
  N12: M1.pin_16, D1.I_C
  N13: M1.pin_17, D1.J_C
  N14: M1.pin_22, M1.pin_23, M1.pin_24, M1.pin_44, R1.Pin_0, R2.Pin_0, R3.Pin_0, R4.Pin_0, R5.Pin_0, R6.Pin_0, R7.Pin_0, R8.Pin_0, R9.Pin_0, R10.Pin_0, R11.Pin_0, R12.Pin_0
  N15: D1.A_A, R3.Pin_1
  N16: D1.B_A, R4.Pin_1
  N17: D1.C_A, R5.Pin_1
  N18: D1.D_A, R6.Pin_1
  N19: D1.E_A, R7.Pin_1
  N20: D1.F_A, R8.Pin_1
  N21: D1.G_A, R9.Pin_1
  N22: D1.H_A, R10.Pin_1
  N23: D1.I_A, R11.Pin_1
  N24: D1.J_A, R12.Pin_1

custom parts:
  ESP32-S3-DevKitC-1: ESP32-S2-DevKitC-1 is an entry-level development board based on ESP32-S2-SOLO (on-board PCB antenna). It is based on the ESP32 microcontroller that boasts Wifi, Bluetooth, Ethernet and Low Power support all in a single chip. (vanepp) Feb 2022: converted to ESP32-S2-DevKitC-1. This module is 44pins long (2x22) and 11 pins width.
