# Fritzing sketch led_bar_tellen (saved by Fritzing 0.9.10b)
breadboards: 3

parts:
  M1 = ESP32-S3-DevKitC-1 [part_number=ESP32-S3-DevKitC-1]
  R1 = Resistor [tolerance=±5% power=0.25 resistance=330 package=THT]
  R2 = Resistor [tolerance=±5% power=0.25 resistance=330 package=THT]
  R3 = Resistor [tolerance=±5% power=0.25 resistance=330 package=THT]
  R4 = Resistor [tolerance=±5% power=0.25 resistance=330 package=THT]
  R5 = Resistor [tolerance=±5% power=0.25 resistance=330 package=THT]
  R6 = Resistor [tolerance=±5% power=0.25 resistance=330 package=THT]
  R7 = Resistor [tolerance=±5% power=0.25 resistance=330 package=THT]
  R8 = Resistor [tolerance=±5% power=0.25 resistance=330 package=THT]
  R9 = Resistor [tolerance=±5% power=0.25 resistance=330 package=THT]
  R10 = Resistor [tolerance=±5% power=0.25 resistance=330 package=THT]
  D1 = LED_BARGRAPH_10 [package=led_bargaph_10]

nets:
  N1: M1.pin_1, M1.pin_2
  N2: M1.pin_5, R1.Pin_1
  N3: M1.pin_6, R2.Pin_1
  N4: M1.pin_7, R3.Pin_1
  N5: M1.pin_8, R4.Pin_1
  N6: M1.pin_9, R5.Pin_1
  N7: M1.pin_10, R6.Pin_1
  N8: M1.pin_11, R7.Pin_1
  N9: M1.pin_12, R8.Pin_1
  N10: M1.pin_13, R9.Pin_1
  N11: M1.pin_14, R10.Pin_1
  N12: M1.pin_22, D1.J_C, D1.I_C, D1.H_C, D1.G_C, D1.F_C, D1.E_C, D1.D_C, D1.C_C, D1.B_C
  N13: R1.Pin_0, D1.A_A
  N14: R2.Pin_0, D1.B_A
  N15: R3.Pin_0, D1.C_A
  N16: R4.Pin_0, D1.D_A
  N17: R5.Pin_0, D1.E_A
  N18: R6.Pin_0, D1.F_A
  N19: R7.Pin_0, D1.G_A
  N20: R8.Pin_0, D1.H_A
  N21: R9.Pin_0, D1.I_A
  N22: R10.Pin_0, D1.J_A

custom parts:
  ESP32-S3-DevKitC-1: ESP32-S2-DevKitC-1 is an entry-level development board based on ESP32-S2-SOLO (on-board PCB antenna). It is based on the ESP32 microcontroller that boasts Wifi, Bluetooth, Ethernet and Low Power support all in a single chip. (vanepp) Feb 2022: converted to ESP32-S2-DevKitC-1. This module is 44pins long (2x22) and 11 pins width.
