# Fritzing sketch lightrider (saved by Fritzing 0.9.10b)
breadboards: 3

parts:
  M1 = ESP32-S3-DevKitC-1 [part_number=ESP32-S3-DevKitC-1]
  R1 = Resistor [tolerance=±5% resistance=330 package="0402 [SMD]"]
  D1 = LED_BARGRAPH_10 [package=led_bargaph_10]
  R2 = Resistor [tolerance=±5% resistance=330 package="0402 [SMD]"]
  R3 = Resistor [tolerance=±5% resistance=330 package="0402 [SMD]"]
  R4 = Resistor [tolerance=±5% resistance=330 package="0402 [SMD]"]
  R5 = Resistor [tolerance=±5% resistance=330 package="0402 [SMD]"]
  R6 = Resistor [tolerance=±5% resistance=330 package="0402 [SMD]"]
  R7 = Resistor [tolerance=±5% resistance=330 package="0402 [SMD]"]
  R8 = Resistor [tolerance=±5% resistance=330 package="0402 [SMD]"]
  R11 = Rotary Potentiometer (Small) [maximum_resistance=100kΩ knob_status=50% power=0.5W package=THT]
  R12 = Resistor [tolerance=±5% resistance=330 package="0402 [SMD]"]
  R13 = Resistor [tolerance=±5% resistance=330 package="0402 [SMD]"]
  R14 = Resistor [tolerance=±5% resistance=330 package="0402 [SMD]"]

nets:
  N1: M1.pin_1, M1.pin_2, R11.leg2
  N2: M1.pin_4, R11.wiper
  N3: M1.pin_5, D1.A_C
  N4: M1.pin_6, D1.B_C
  N5: M1.pin_7, D1.C_C
  N6: M1.pin_8, D1.D_C
  N7: M1.pin_9, D1.E_C
  N8: M1.pin_10, D1.F_C
  N9: M1.pin_11, D1.G_C
  N10: M1.pin_12, D1.H_C
  N11: M1.pin_13, D1.I_C
  N12: M1.pin_14, D1.J_C
  N13: M1.pin_22, M1.pin_23, M1.pin_24, M1.pin_44, R1.Pin_0, R2.Pin_0, R3.Pin_0, R4.Pin_0, R5.Pin_0, R6.Pin_0, R7.Pin_0, R8.Pin_0, R12.Pin_0, R13.Pin_0, R14.Pin_1
  N14: R1.Pin_1, D1.A_A
  N15: D1.B_A, R2.Pin_1
  N16: D1.C_A, R3.Pin_1
  N17: D1.D_A, R4.Pin_1
  N18: D1.E_A, R5.Pin_1
  N19: D1.F_A, R6.Pin_1
  N20: D1.G_A, R7.Pin_1
  N21: D1.H_A, R8.Pin_1
  N22: D1.I_A, R12.Pin_1
  N23: D1.J_A, R13.Pin_1
  N24: R11.leg1, R14.Pin_0

custom parts:
  ESP32-S3-DevKitC-1: ESP32-S2-DevKitC-1 is an entry-level development board based on ESP32-S2-SOLO (on-board PCB antenna). It is based on the ESP32 microcontroller that boasts Wifi, Bluetooth, Ethernet and Low Power support all in a single chip. (vanepp) Feb 2022: converted to ESP32-S2-DevKitC-1. This module is 44pins long (2x22) and 11 pins width.
