# Fritzing sketch pong (saved by Fritzing 0.9.10b)
breadboards: 3

parts:
  M1 = ESP32-S3-DevKitC-1 [part_number=ESP32-S3-DevKitC-1]
  D1 = LED_BARGRAPH_10 [package=led_bargaph_10]
  R1 = Resistor [tolerance=±5% resistance=330 package="0603 [SMD]"]
  R2 = Resistor [tolerance=±5% resistance=330 package="0603 [SMD]"]
  R3 = Resistor [tolerance=±5% resistance=330 package="0603 [SMD]"]
  R4 = Resistor [tolerance=±5% resistance=330 package="0603 [SMD]"]
  R5 = Resistor [tolerance=±5% resistance=330 package="0603 [SMD]"]
  R6 = Resistor [tolerance=±5% resistance=330 package="0603 [SMD]"]
  R7 = Resistor [tolerance=±5% resistance=330 package="0603 [SMD]"]
  R8 = Resistor [tolerance=±5% resistance=330 package="0603 [SMD]"]
  R9 = Resistor [tolerance=±5% resistance=330 package="0603 [SMD]"]
  R10 = Resistor [tolerance=±5% resistance=330 package="0603 [SMD]"]
  LED1 = smd LED [color="Blue (430nm)" package="0805 [SMD]"]
  LED2 = smd LED [color="Green (555nm)" package="0805 [SMD]"]
  LED3 = smd LED [color="Yellow (585nm)" package="0805 [SMD]"]
  LED4 = smd LED [color="Orange (620nm)" package="0805 [SMD]"]
  LED5 = smd LED [color="Red (633nm)" package="0805 [SMD]"]
  R11 = Resistor [tolerance=±5% resistance=330 package="0603 [SMD]"]
  R12 = Resistor [tolerance=±5% resistance=330 package="0603 [SMD]"]
  R13 = Resistor [tolerance=±5% resistance=330 package="0603 [SMD]"]
  R14 = Resistor [tolerance=±5% resistance=330 package="0603 [SMD]"]
  R15 = Resistor [tolerance=±5% resistance=330 package="0603 [SMD]"]
  LED6 = smd LED [color="Green (555nm)" package="0805 [SMD]"]
  R16 = Resistor [tolerance=±5% resistance=330 package="0603 [SMD]"]
  S1 = Pushbutton [package="[SMD]"]
  R17 = Resistor [tolerance=±5% resistance=330 package="0603 [SMD]"]
  7_Segment_4_Digit_Display1 = 7-SEGMENT-4DIGIT common cathode [part_number=HS420561K-32 package=7-segment-4digit-cathode]

nets:
  N1: M1.pin_1, M1.pin_2, S1.Pin_3, S1.Pin_4
  N2: M1.pin_4, D1.A_C
  N3: M1.pin_5, D1.B_C
  N4: M1.pin_6, D1.C_C
  N5: M1.pin_7, D1.D_C
  N6: M1.pin_8, D1.E_C
  N7: M1.pin_9, D1.F_C
  N8: M1.pin_10, D1.G_C
  N9: M1.pin_11, D1.H_C
  N10: M1.pin_12, D1.I_C
  N11: M1.pin_13, D1.J_C
  N12: M1.pin_14, S1.Pin_1, S1.Pin_2, R17.Pin_1
  N13: M1.pin_15, LED6.anode
  N14: M1.pin_16, LED5.anode
  N15: M1.pin_17, LED4.anode
  N16: M1.pin_18, LED3.anode
  N17: M1.pin_19, LED2.anode
  N18: M1.pin_20, LED1.anode
  N19: M1.pin_22, M1.pin_23, M1.pin_24, M1.pin_44, R1.Pin_0, R2.Pin_0, R3.Pin_0, R4.Pin_0, R5.Pin_0, R6.Pin_0, R7.Pin_0, R8.Pin_0, R9.Pin_0, R10.Pin_0, R11.Pin_1, R12.Pin_1, R13.Pin_1, R14.Pin_1, R15.Pin_1, R16.Pin_0, R17.Pin_0
  N20: M1.pin_27, 7_Segment_4_Digit_Display1.pin_3
  N21: M1.pin_28, 7_Segment_4_Digit_Display1.pin_5
  N22: M1.pin_29, 7_Segment_4_Digit_Display1.pin_10
  N23: M1.pin_30, 7_Segment_4_Digit_Display1.pin_1
  N24: M1.pin_31, 7_Segment_4_Digit_Display1.pin_2
  N25: M1.pin_32, 7_Segment_4_Digit_Display1.pin_4
  N26: M1.pin_33, 7_Segment_4_Digit_Display1.pin_7
  N27: M1.pin_34, 7_Segment_4_Digit_Display1.pin_11
  N28: M1.pin_40, 7_Segment_4_Digit_Display1.pin_9
  N29: M1.pin_41, 7_Segment_4_Digit_Display1.pin_12
  N30: LED1.cathode, R11.Pin_0
  N31: LED2.cathode, R12.Pin_0
  N32: LED3.cathode, R13.Pin_0
  N33: LED4.cathode, R14.Pin_0
  N34: LED5.cathode, R15.Pin_0
  N35: LED6.cathode, R16.Pin_1

custom parts:
  ESP32-S3-DevKitC-1: ESP32-S2-DevKitC-1 is an entry-level development board based on ESP32-S2-SOLO (on-board PCB antenna). It is based on the ESP32 microcontroller that boasts Wifi, Bluetooth, Ethernet and Low Power support all in a single chip. (vanepp) Feb 2022: converted to ESP32-S2-DevKitC-1. This module is 44pins long (2x22) and 11 pins width.
  7-SEGMENT-4DIGIT common cathode: A 7 Segment 4 Digit common cathode display, with decimal points
