# Fritzing sketch verkeerslicht (saved by Fritzing 0.9.10b)
breadboards: 3

parts:
  M1 = ESP32-S3-DevKitC-1 [part_number=ESP32-S3-DevKitC-1]
  S1 = Pushbutton [package="[THT]"]
  R1 = Resistor [tolerance=±5% resistance=330 package="0402 [SMD]"]
  LED1 = smd LED [color="Red (633nm)" package="1206 [SMD]"]
  LED2 = smd LED [color="Yellow (592nm)" package="1206 [SMD]"]
  LED3 = smd LED [color="Green (570nm)" package="1206 [SMD]"]
  R2 = Resistor [tolerance=±5% resistance=330 package="0402 [SMD]"]

nets:
  N1: M1.pin_1, M1.pin_2, S1.Pin_1, S1.Pin_2, R2.Pin_1
  N2: M1.pin_5, LED1.anode
  N3: M1.pin_6, LED2.anode
  N4: M1.pin_7, LED3.anode
  N5: M1.pin_11, S1.Pin_3, S1.Pin_4, R1.Pin_1
  N6: M1.pin_22, M1.pin_23, M1.pin_24, M1.pin_44, R1.Pin_0
  N7: LED1.cathode, LED2.cathode, LED3.cathode, R2.Pin_0

custom parts:
  ESP32-S3-DevKitC-1: ESP32-S2-DevKitC-1 is an entry-level development board based on ESP32-S2-SOLO (on-board PCB antenna). It is based on the ESP32 microcontroller that boasts Wifi, Bluetooth, Ethernet and Low Power support all in a single chip. (vanepp) Feb 2022: converted to ESP32-S2-DevKitC-1. This module is 44pins long (2x22) and 11 pins width.
